// Logisim project cpu.circ as structural Verilog: 8 circuits, main circuit main
module main (
  input  [31:0] INSTRUCTION,
  input  CLOCK,
  output [31:0] FETCH_ADDRESS,
  output [31:0] ra,
  output [31:0] sp,
  output [31:0] t0,
  output [31:0] t1,
  output [31:0] t2,
  output [31:0] s0,
  output [31:0] s1,
  output [31:0] a0
);

  wire execute_1_memrw, execute_1_pcsel, instruction_decoder_1_writeenable;
  wire [1:0] execute_1_wbsel;
  wire [3:0] execute_1_alusel;
  wire [4:0] instruction_decoder_1_rd, instruction_decoder_1_rs1, instruction_decoder_1_rs2;
  wire [31:0] adder_1_out, alu_1_result, DMEM_p5, execute_1_a, execute_1_b, IMMEDIATE, INSTRUCTION_POST,
       multiplexer_1_out, multiplexer_3_out, PC1, PC2, RegFile_read_data_1, RegFile_read_data_2,
       subtractor_1_out;

  Multiplexer #(.width(32), .enable("false")) multiplexer_1 (
    .in0(INSTRUCTION), .in1(32'h13), .out(multiplexer_1_out), .sel(execute_1_pcsel));
  Register #(.width(32)) PC (.D(PC2), .en(1'b1), .clk(CLOCK), .Q(PC1));  // open: clr
  Register #(.width(32)) INSTRUCTION_REG (
    .D(multiplexer_1_out), .en(1'b1), .clk(CLOCK), .Q(INSTRUCTION_POST));  // open: clr
  Shifter #(.width(32), .shift("ar")) shifter_1 (.in(PC1), .\dist (5'b00010), .out(FETCH_ADDRESS));
  instruction_decoder instruction_decoder_1 (
    .INSTRUCTION(INSTRUCTION_POST), .IMMEDIATE(IMMEDIATE), .RD(instruction_decoder_1_rd),
    .RS1(instruction_decoder_1_rs1), .RS2(instruction_decoder_1_rs2),
    .WriteEnable(instruction_decoder_1_writeenable));
  regfile_main RegFile (
    .rs2(instruction_decoder_1_rs2), .rd(instruction_decoder_1_rd), .Read_Data_1(RegFile_read_data_1),
    .Read_Data_2(RegFile_read_data_2), .ra(ra), .sp(sp), .t0(t0), .t1(t1), .t2(t2), .s0(s0), .s1(s1),
    .a0(a0), .rs1(instruction_decoder_1_rs1), .Write_Data(multiplexer_3_out),
    .RegWEn(instruction_decoder_1_writeenable), .clk(CLOCK));
  Subtractor #(.width(32)) subtractor_1 (.a(PC1), .b(32'h4), .out(subtractor_1_out));  // open: bin, bout
  execute execute_1 (
    .PC(subtractor_1_out), .rs1(RegFile_read_data_1), .rs2(RegFile_read_data_2), .imm(IMMEDIATE),
    .Instruction(INSTRUCTION_POST), .A(execute_1_a), .B(execute_1_b), .WBSel(execute_1_wbsel),
    .ALUSel(execute_1_alusel), .MemRW(execute_1_memrw), .PCsel(execute_1_pcsel));
  alu alu_1 (.A(execute_1_a), .B(execute_1_b), .ALUSel(execute_1_alusel), .Result(alu_1_result));
  Adder #(.width(32)) adder_1 (.a(PC1), .b(32'h4), .out(adder_1_out));  // open: cin, cout
  Multiplexer #(.width(32), .enable("false")) multiplexer_2 (
    .in0(adder_1_out), .in1(alu_1_result), .out(PC2), .sel(execute_1_pcsel));
  Multiplexer #(.select(2), .width(32), .enable("false")) multiplexer_3 (
    .in0(PC1), .in1(alu_1_result), .in2(DMEM_p5), .out(multiplexer_3_out), .sel(execute_1_wbsel));  // open: in3
  // mem_main DMEM: pin names not known; wires that end beside it: alu_1_result, RegFile_read_data_2, execute_1_memrw, CLOCK, DMEM_p5

  // Other names for the same wires on the sheet: clk = CLOCK; fetch_addr[31:0] = FETCH_ADDRESS

  // Notes on the sheet:
  //   Output
  //   Inputs/Outputs from run.circ. DO NOT MOVE THESE.
  //   Inputs
  //   Inputs/Outputs from run.circ. DO NOT MOVE THESE.
endmodule

module instruction_splitter (
  input  [31:0] INSTRUCTION,
  output [3:0] imm41,
  output [6:0] OPCODE,
  output [19:0] imm3112,
  output imm11b,
  output [4:0] RD,
  output [4:0] imm40,
  output [7:0] imm1912,
  output [2:0] funct3,
  output [4:0] rs1,
  output [11:0] imm110,
  output [5:0] imm105,
  output [4:0] rs2,
  output [6:0] funct7,
  output [6:0] imm115,
  output imm12,
  output imm11j,
  output [9:0] imm101,
  output imm20
);


  assign funct3 = INSTRUCTION[14:12];
  assign funct7 = INSTRUCTION[31:25];
  assign imm11b = INSTRUCTION[7];
  assign imm11j = INSTRUCTION[20];
  assign imm12 = INSTRUCTION[31];
  assign imm20 = INSTRUCTION[31];
  assign imm40 = INSTRUCTION[11:7];
  assign imm41 = INSTRUCTION[11:8];
  assign imm101 = INSTRUCTION[30:21];
  assign imm105 = INSTRUCTION[30:25];
  assign imm110 = INSTRUCTION[31:20];
  assign imm115 = INSTRUCTION[31:25];
  assign imm1912 = INSTRUCTION[19:12];
  assign imm3112 = INSTRUCTION[31:12];
  assign OPCODE = INSTRUCTION[6:0];
  assign RD = INSTRUCTION[11:7];
  assign rs1 = INSTRUCTION[19:15];
  assign rs2 = INSTRUCTION[24:20];
endmodule

module instruction_decoder (
  input  [31:0] INSTRUCTION,
  output [31:0] IMMEDIATE,
  output [4:0] RD,
  output [4:0] RS1,
  output [4:0] RS2,
  output WriteEnable
);

  wire or_1_out, SBType, SType;
  wire [6:0] OPCODE;

  Comparator #(.width(7), .mode("unsigned")) comparator_1 (.a(OPCODE), .b(7'b0100011), .eq(SType));  // open: gt, lt
  Comparator #(.width(7), .mode("unsigned")) comparator_2 (.a(OPCODE), .b(7'b1100011), .eq(SBType));  // open: gt, lt
  or or_1 (or_1_out, SType, SBType);
  instruction_splitter instruction_splitter_1 (
    .INSTRUCTION(INSTRUCTION), .OPCODE(OPCODE), .RD(RD), .rs1(RS1), .rs2(RS2));  // open: imm41, imm3112, imm11b, imm40, imm1912, funct3, imm110, imm105, funct7, imm115, imm12, imm11j, imm101, imm20
  not not_1 (WriteEnable, or_1_out);
  imm_gen imm_gen_1 (.INSTRUCTION(INSTRUCTION), .IMMEDIATE(IMMEDIATE));
endmodule

module alu_sel (
  input  [31:0] INSTRUCTION,
  output [3:0] ALUSel
);

  wire and_1_out, and_2_out, and_3_out, and_4_out, and_5_out, and_6_out, and_7_out, and_8_out, and_9_out,
       and_10_out, comparator_1_eq, comparator_2_eq, comparator_3_eq, comparator_4_eq, comparator_5_eq,
       comparator_6_eq, comparator_7_eq, comparator_16_eq, comparator_17_eq, comparator_18_eq,
       comparator_19_eq, comparator_20_eq, comparator_21_eq, comparator_22_eq, comparator_23_eq,
       comparator_24_eq, comparator_25_eq, comparator_26_eq, comparator_27_eq, IType1, IType2, IType3,
       not_1_out, not_2_out, or_1_out, or_2_out, or_3_out, or_4_out, RType, SBType, SType, UJType, UType;
  wire [2:0] FUNCT3;
  wire [3:0] multiplexer_7_out, NotAddSel;
  wire [6:0] FUNCT7, OPCODE;

  Comparator #(.width(3), .mode("unsigned")) comparator_1 (
    .a(FUNCT3), .b(3'b111), .eq(comparator_1_eq));  // open: gt, lt
  Comparator #(.width(3), .mode("unsigned")) comparator_2 (
    .a(FUNCT3), .b(3'b010), .eq(comparator_2_eq));  // open: gt, lt
  Comparator #(.width(3), .mode("unsigned")) comparator_3 (
    .a(FUNCT3), .b(3'b011), .eq(comparator_3_eq));  // open: gt, lt
  Comparator #(.width(3), .mode("unsigned")) comparator_4 (
    .a(FUNCT3), .b(3'b100), .eq(comparator_4_eq));  // open: gt, lt
  Comparator #(.width(3), .mode("unsigned")) comparator_5 (
    .a(FUNCT3), .b(3'b110), .eq(comparator_5_eq));  // open: gt, lt
  Comparator #(.width(7), .mode("unsigned")) comparator_6 (
    .a(FUNCT7), .b(7'b0000001), .eq(comparator_6_eq));  // open: gt, lt
  Comparator #(.width(7), .mode("unsigned")) comparator_7 (
    .a(FUNCT7), .b({7{1'b0}}), .eq(comparator_7_eq));  // open: gt, lt
  instruction_splitter instruction_splitter_1 (
    .INSTRUCTION(INSTRUCTION), .OPCODE(OPCODE), .funct3(FUNCT3), .funct7(FUNCT7));  // open: imm41, imm3112, imm11b, RD, imm40, imm1912, rs1, imm110, imm105, rs2, imm115, imm12, imm11j, imm101, imm20
  Comparator #(.width(7), .mode("unsigned")) comparator_8 (.a(OPCODE), .b(7'b0110011), .eq(RType));  // open: gt, lt
  Comparator #(.width(7), .mode("unsigned")) comparator_9 (.a(OPCODE), .b(7'b0000011), .eq(IType1));  // open: gt, lt
  Comparator #(.width(7), .mode("unsigned")) comparator_10 (.a(OPCODE), .b(7'b0010011), .eq(IType2));  // open: gt, lt
  Comparator #(.width(7), .mode("unsigned")) comparator_11 (.a(OPCODE), .b(7'b0100011), .eq(SType));  // open: gt, lt
  Comparator #(.width(7), .mode("unsigned")) comparator_12 (.a(OPCODE), .b(7'b1100011), .eq(SBType));  // open: gt, lt
  Comparator #(.width(7), .mode("unsigned")) comparator_13 (.a(OPCODE), .b(7'b0110111), .eq(UType));  // open: gt, lt
  Comparator #(.width(7), .mode("unsigned")) comparator_14 (.a(OPCODE), .b(7'b1101111), .eq(UJType));  // open: gt, lt
  Comparator #(.width(7), .mode("unsigned")) comparator_15 (.a(OPCODE), .b(7'b1100111), .eq(IType3));  // open: gt, lt
  Multiplexer #(.width(4), .enable("false")) multiplexer_1 (
    .in1(4'b0111), .out(NotAddSel), .sel(comparator_2_eq));  // open: in0
  Multiplexer #(.width(4), .enable("false")) multiplexer_2 (
    .in1(4'b1011), .out(NotAddSel), .sel(comparator_3_eq));  // open: in0
  Multiplexer #(.width(4), .enable("false")) multiplexer_3 (
    .in1(4'b0011), .out(NotAddSel), .sel(comparator_4_eq));  // open: in0
  Multiplexer #(.width(4), .enable("false")) multiplexer_4 (
    .in1(4'b0010), .out(NotAddSel), .sel(comparator_5_eq));  // open: in0
  and and_1 (and_1_out, comparator_1_eq, comparator_6_eq);
  Multiplexer #(.width(4), .enable("false")) multiplexer_5 (
    .in1(4'b0001), .out(NotAddSel), .sel(or_1_out));  // open: in0
  and and_2 (and_2_out, comparator_1_eq, comparator_7_eq);
  or or_1 (or_1_out, and_2_out, IType2);
  Multiplexer #(.width(4), .enable("false")) multiplexer_6 (
    .in1(4'b1001), .out(NotAddSel), .sel(and_1_out));  // open: in0
  Comparator #(.width(3), .mode("unsigned")) comparator_16 (
    .a(FUNCT3), .b(3'b000), .eq(comparator_16_eq));  // open: gt, lt
  not not_1 (not_1_out, RType);
  Comparator #(.width(7), .mode("unsigned")) comparator_17 (
    .a(FUNCT7), .b({7{1'b0}}), .eq(comparator_17_eq));  // open: gt, lt
  Comparator #(.width(3), .mode("unsigned")) comparator_18 (
    .a(FUNCT3), .b(3'b000), .eq(comparator_18_eq));  // open: gt, lt
  and and_3 (and_3_out, comparator_16_eq, or_2_out);
  or or_2 (or_2_out, not_1_out, comparator_17_eq);
  or or_3 (or_3_out, RType, IType2);
  Comparator #(.width(7), .mode("unsigned")) comparator_19 (
    .a(FUNCT7), .b(7'b0000001), .eq(comparator_19_eq));  // open: gt, lt
  Comparator #(.width(7), .mode("unsigned")) comparator_20 (
    .a(FUNCT7), .b(7'b0100000), .eq(comparator_20_eq));  // open: gt, lt
  Comparator #(.width(3), .mode("unsigned")) comparator_21 (
    .a(FUNCT3), .b(3'b001), .eq(comparator_21_eq));  // open: gt, lt
  Comparator #(.width(7), .mode("unsigned")) comparator_22 (
    .a(FUNCT7), .b({7{1'b0}}), .eq(comparator_22_eq));  // open: gt, lt
  Comparator #(.width(7), .mode("unsigned")) comparator_23 (
    .a(FUNCT7), .b(7'b0000001), .eq(comparator_23_eq));  // open: gt, lt
  Comparator #(.width(3), .mode("unsigned")) comparator_24 (
    .a(FUNCT3), .b(3'b101), .eq(comparator_24_eq));  // open: gt, lt
  Comparator #(.width(7), .mode("unsigned")) comparator_25 (
    .a(FUNCT7), .b({7{1'b0}}), .eq(comparator_25_eq));  // open: gt, lt
  Comparator #(.width(7), .mode("unsigned")) comparator_26 (
    .a(FUNCT7), .b(7'b0000001), .eq(comparator_26_eq));  // open: gt, lt
  Comparator #(.width(7), .mode("unsigned")) comparator_27 (
    .a(FUNCT7), .b(7'b0100000), .eq(comparator_27_eq));  // open: gt, lt
  Multiplexer #(.width(4), .enable("false")) multiplexer_7 (
    .in0(NotAddSel), .in1(4'b0000), .out(multiplexer_7_out), .sel(or_4_out));
  or or_4 (or_4_out, and_3_out, not_2_out);
  not not_2 (not_2_out, or_3_out);
  and and_4 (and_4_out, comparator_18_eq, comparator_19_eq);
  Multiplexer #(.width(4), .enable("false")) multiplexer_8 (
    .in1(4'b1100), .out(NotAddSel), .sel(and_5_out));  // open: in0
  and and_5 (and_5_out, comparator_18_eq, comparator_20_eq);
  and and_6 (and_6_out, comparator_21_eq, comparator_22_eq);
  and and_7 (and_7_out, comparator_21_eq, comparator_23_eq);
  and and_8 (and_8_out, comparator_24_eq, comparator_25_eq);
  and and_9 (and_9_out, comparator_24_eq, comparator_26_eq);
  and and_10 (and_10_out, comparator_24_eq, comparator_27_eq);
  Multiplexer #(.width(4), .enable("false")) multiplexer_9 (
    .in1(4'b1010), .out(NotAddSel), .sel(and_4_out));  // open: in0
  Multiplexer #(.width(4), .enable("false")) multiplexer_10 (
    .in1(4'b0110), .out(NotAddSel), .sel(and_6_out));  // open: in0
  Multiplexer #(.width(4), .enable("false")) multiplexer_11 (
    .in1(4'b1110), .out(NotAddSel), .sel(and_7_out));  // open: in0
  Multiplexer #(.width(4), .enable("false")) multiplexer_12 (
    .in1(4'b0100), .out(NotAddSel), .sel(and_8_out));  // open: in0
  Multiplexer #(.width(4), .enable("false")) multiplexer_13 (
    .in1(4'b1000), .out(NotAddSel), .sel(and_9_out));  // open: in0
  Multiplexer #(.width(4), .enable("false")) multiplexer_14 (
    .in1(4'b0101), .out(NotAddSel), .sel(and_10_out));  // open: in0
  Multiplexer #(.width(4), .enable("false")) multiplexer_15 (
    .in0(multiplexer_7_out), .in1(4'b1101), .out(ALUSel), .sel(UType));
endmodule

module imm_gen (
  input  [31:0] INSTRUCTION,
  output [31:0] IMMEDIATE
);

  wire imm11b, imm11j, imm12, imm20, IType, IType1, IType2, IType3, or_2_out, RType, SBType, SType, UJType,
       UType;
  wire [2:0] funct3;
  wire [3:0] imm41;
  wire [4:0] imm40, rd, rs1, rs2;
  wire [5:0] imm105;
  wire [6:0] funct7, imm115, OPCODE;
  wire [7:0] imm1219, imm1912;
  wire [9:0] imm101;
  wire [11:0] imm110;
  wire [19:0] imm3112;
  wire [31:0] bit_extender_1_out, bit_extender_2_out, bit_extender_3_out, bit_extender_4_out,
       multiplexer_1_out, multiplexer_2_out, multiplexer_3_out, multiplexer_4_out, undriven;

  or or_1 (IType, IType3, or_2_out);
  or or_2 (or_2_out, IType1, IType2);
  Comparator #(.width(7), .mode("unsigned")) comparator_1 (.a(OPCODE), .b(7'b0110011), .eq(RType));  // open: gt, lt
  Comparator #(.width(7), .mode("unsigned")) comparator_2 (.a(OPCODE), .b(7'b0000011), .eq(IType1));  // open: gt, lt
  Comparator #(.width(7), .mode("unsigned")) comparator_3 (.a(OPCODE), .b(7'b0010011), .eq(IType2));  // open: gt, lt
  Comparator #(.width(7), .mode("unsigned")) comparator_4 (.a(OPCODE), .b(7'b0100011), .eq(SType));  // open: gt, lt
  Comparator #(.width(7), .mode("unsigned")) comparator_5 (.a(OPCODE), .b(7'b1100011), .eq(SBType));  // open: gt, lt
  Comparator #(.width(7), .mode("unsigned")) comparator_6 (.a(OPCODE), .b(7'b0110111), .eq(UType));  // open: gt, lt
  Comparator #(.width(7), .mode("unsigned")) comparator_7 (.a(OPCODE), .b(7'b1101111), .eq(UJType));  // open: gt, lt
  Comparator #(.width(7), .mode("unsigned")) comparator_8 (.a(OPCODE), .b(7'b1100111), .eq(IType3));  // open: gt, lt
  instruction_splitter instruction_splitter_1 (
    .INSTRUCTION(INSTRUCTION), .imm41(imm41), .OPCODE(OPCODE), .imm3112(imm3112), .imm11b(imm11b), .RD(rd),
    .imm40(imm40), .imm1912(imm1912), .funct3(funct3), .rs1(rs1), .imm110(imm110), .imm105(imm105),
    .rs2(rs2), .funct7(funct7), .imm115(imm115), .imm12(imm12), .imm11j(imm11j), .imm101(imm101),
    .imm20(imm20));
  assign bit_extender_1_out = {{11{imm20}}, {imm20, imm1219, imm11j, imm101, 1'b0}};  // Bit_Extender bit_extender_1
  assign bit_extender_2_out = {{19{imm12}}, {imm12, imm11b, imm105, imm41, 1'b0}};  // Bit_Extender bit_extender_2
  assign bit_extender_3_out = {{20{imm115[6]}}, {imm115, imm40}};  // Bit_Extender bit_extender_3
  Multiplexer #(.width(32), .enable("false")) multiplexer_1 (
    .in0(undriven), .in1(bit_extender_1_out), .out(multiplexer_1_out), .sel(UJType));
  Multiplexer #(.width(32), .enable("false")) multiplexer_2 (
    .in0(multiplexer_1_out), .in1({imm3112, {12{1'b0}}}), .out(multiplexer_2_out), .sel(UType));
  Multiplexer #(.width(32), .enable("false")) multiplexer_3 (
    .in0(multiplexer_2_out), .in1(bit_extender_2_out), .out(multiplexer_3_out), .sel(SBType));
  assign bit_extender_4_out = {{20{imm110[11]}}, imm110};  // Bit_Extender bit_extender_4
  Multiplexer #(.width(32), .enable("false")) multiplexer_4 (
    .in0(multiplexer_3_out), .in1(bit_extender_3_out), .out(multiplexer_4_out), .sel(SType));
  Multiplexer #(.width(32), .enable("false")) multiplexer_5 (
    .in0(multiplexer_4_out), .in1(bit_extender_4_out), .out(IMMEDIATE), .sel(IType));
endmodule

module execute (
  input  [31:0] PC,
  input  [31:0] rs1,
  input  [31:0] rs2,
  input  [31:0] imm,
  input  [31:0] Instruction,
  output [31:0] A,
  output [31:0] B,
  output [1:0] WBSel,
  output [3:0] ALUSel,
  output MemRW,
  output PCsel
);

  wire and_1_out, and_2_out, and_3_out, and_4_out, and_5_out, and_6_out, and_7_out, ASel, BrEq, BrLt, BrUn,
       BSel, comparator_2_eq, comparator_3_eq, comparator_4_eq, comparator_5_eq, comparator_6_lt,
       comparator_7_lt, instruction_type_1_itype3, instruction_type_1_rtype, instruction_type_1_ujtype,
       instruction_type_1_utype, IType1, not_2_out, not_3_out, not_4_out, or_3_out, or_5_out, or_6_out,
       or_8_out, SBType, UJorI, UorUJ;
  wire [1:0] multiplexer_3_out;
  wire [2:0] FUNCT3;

  Multiplexer #(.width(32), .enable("false")) multiplexer_1 (.in0(rs1), .in1(PC), .out(A), .sel(ASel));
  Multiplexer #(.width(32), .enable("false")) multiplexer_2 (.in0(rs2), .in1(imm), .out(B), .sel(BSel));
  instruction_splitter instruction_splitter_1 (
    .INSTRUCTION(Instruction), .funct3(FUNCT3));  // open: imm41, OPCODE, imm3112, imm11b, RD, imm40, imm1912, rs1, imm110, imm105, rs2, funct7, imm115, imm12, imm11j, imm101, imm20
  alu_sel alu_sel_1 (.INSTRUCTION(Instruction), .ALUSel(ALUSel));
  instruction_type instruction_type_1 (
    .INSTRUCTION(Instruction), .RType(instruction_type_1_rtype), .IType1(IType1), .SType(MemRW),
    .SBType(SBType), .UType(instruction_type_1_utype), .UJType(instruction_type_1_ujtype),
    .IType3(instruction_type_1_itype3));  // open: IType2
  not not_1 (BSel, instruction_type_1_rtype);
  or or_1 (UJorI, instruction_type_1_ujtype, instruction_type_1_itype3);
  Comparator #(.width(3), .mode("unsigned")) comparator_1 (.a(FUNCT3), .b(3'b110), .eq(BrUn));  // open: gt, lt
  or or_2 (UorUJ, instruction_type_1_utype, instruction_type_1_ujtype);
  Multiplexer #(.width(2), .enable("false")) multiplexer_3 (
    .in0(2'b01), .in1(2'b00), .out(multiplexer_3_out), .sel(UJorI));
  or or_3 (or_3_out, IType1, SBType);
  Multiplexer #(.width(2), .enable("false")) multiplexer_4 (
    .in0(multiplexer_3_out), .in1(2'b10), .out(WBSel), .sel(IType1));
  not not_2 (not_2_out, or_3_out);
  or or_4 (ASel, UorUJ, SBType);
  Comparator #(.width(3), .mode("unsigned")) comparator_2 (
    .a(FUNCT3), .b(3'b000), .eq(comparator_2_eq));  // open: gt, lt
  Comparator #(.width(3), .mode("unsigned")) comparator_3 (
    .a(FUNCT3), .b(3'b100), .eq(comparator_3_eq));  // open: gt, lt
  Comparator #(.width(3), .mode("unsigned")) comparator_4 (
    .a(FUNCT3), .b(3'b110), .eq(comparator_4_eq));  // open: gt, lt
  Comparator #(.width(3), .mode("unsigned")) comparator_5 (
    .a(FUNCT3), .b(3'b001), .eq(comparator_5_eq));  // open: gt, lt
  not not_3 (not_3_out, BrEq);
  Comparator #(.width(32), .mode("unsigned")) comparator_6 (.a(rs1), .b(rs2), .lt(comparator_6_lt));  // open: gt, eq
  Comparator #(.width(32)) comparator_7 (.a(rs1), .b(rs2), .eq(BrEq), .lt(comparator_7_lt));  // open: gt
  and and_1 (and_1_out, comparator_2_eq, BrEq);
  and and_2 (and_2_out, comparator_3_eq, BrLt);
  and and_3 (and_3_out, comparator_4_eq, BrLt);
  and and_4 (and_4_out, comparator_5_eq, not_3_out);
  and and_5 (and_5_out, comparator_6_lt, BrUn);
  not not_4 (not_4_out, BrUn);
  or or_5 (or_5_out, and_1_out, and_2_out);
  or or_6 (or_6_out, and_3_out, and_4_out);
  or or_7 (BrLt, and_5_out, and_6_out);
  and and_6 (and_6_out, not_4_out, comparator_7_lt);
  or or_8 (or_8_out, or_5_out, or_6_out);
  and and_7 (and_7_out, or_8_out, SBType);
  or or_9 (PCsel, and_7_out, UJorI);

  // Other names for the same wires on the sheet: SType = MemRW
endmodule

module instruction_type (
  input  [31:0] INSTRUCTION,
  output RType,
  output IType1,
  output IType2,
  output SType,
  output SBType,
  output UType,
  output UJType,
  output IType3
);

  wire [2:0] FUNCT3;
  wire [6:0] FUNCT7, OPCODE;

  instruction_splitter instruction_splitter_1 (
    .INSTRUCTION(INSTRUCTION), .OPCODE(OPCODE), .funct3(FUNCT3), .funct7(FUNCT7));  // open: imm41, imm3112, imm11b, RD, imm40, imm1912, rs1, imm110, imm105, rs2, imm115, imm12, imm11j, imm101, imm20
  Comparator #(.width(7), .mode("unsigned")) comparator_1 (.a(OPCODE), .b(7'b0110011), .eq(RType));  // open: gt, lt
  Comparator #(.width(7), .mode("unsigned")) comparator_2 (.a(OPCODE), .b(7'b0000011), .eq(IType1));  // open: gt, lt
  Comparator #(.width(7), .mode("unsigned")) comparator_3 (.a(OPCODE), .b(7'b0010011), .eq(IType2));  // open: gt, lt
  Comparator #(.width(7), .mode("unsigned")) comparator_4 (.a(OPCODE), .b(7'b0100011), .eq(SType));  // open: gt, lt
  Comparator #(.width(7), .mode("unsigned")) comparator_5 (.a(OPCODE), .b(7'b1100011), .eq(SBType));  // open: gt, lt
  Comparator #(.width(7), .mode("unsigned")) comparator_6 (.a(OPCODE), .b(7'b0110111), .eq(UType));  // open: gt, lt
  Comparator #(.width(7), .mode("unsigned")) comparator_7 (.a(OPCODE), .b(7'b1101111), .eq(UJType));  // open: gt, lt
  Comparator #(.width(7), .mode("unsigned")) comparator_8 (.a(OPCODE), .b(7'b1100111), .eq(IType3));  // open: gt, lt
endmodule

module fix_load (
  input  [31:0] INSTRUCTION,
  input  [31:0] lwin,
  input  [31:0] offset,
  output [31:0] lwout
);

  wire [2:0] instruction_splitter_1_funct3;
  wire [31:0] lb, lh;

  instruction_splitter instruction_splitter_1 (
    .INSTRUCTION(INSTRUCTION), .funct3(instruction_splitter_1_funct3));  // open: imm41, OPCODE, imm3112, imm11b, RD, imm40, imm1912, rs1, imm110, imm105, rs2, funct7, imm115, imm12, imm11j, imm101, imm20
  Multiplexer #(.select(3), .width(32), .enable("false")) multiplexer_1 (
    .in0(lb), .in1(lh), .in2(lwin), .out(lwout), .sel(instruction_splitter_1_funct3));  // open: in3, in4, in5, in6, in7

  // Other names for the same wires on the sheet: lw[31:0] = lwin
endmodule
