// Logisim project alu-back2.circ as structural Verilog: 1 circuit, main circuit alu
module alu (
  input  [31:0] A,
  input  [31:0] B,
  input  [3:0] ALUSel,
  output [31:0] Result,
  output [31:0] out_5,
  output [31:0] out_6,
  output [31:0] out_7,
  output [31:0] out_8
);

  wire [0:0] slt;
  wire [4:0] bitselector_1_out, bitselector_2_out, bitselector_3_out;
  wire [30:0] sub;
  wire [31:0] add, adder_1_out, and1, divu, mulhu, multiplexer_1_out, negator_1_out, negator_2_out,
       negator_4_out, or1, remu, sll1, sra1, srl1, xor1;

  Negator #(.width(32)) negator_1 (.in(A), .out(negator_1_out));
  Adder #(.width(32)) adder_1 (.a(B), .b(A), .out(adder_1_out));  // open: cin, cout
  BitSelector #(.width(32), .group(5)) bitselector_1 (.in(B), .out(bitselector_1_out), .sel(3'b000));
  BitSelector #(.width(32), .group(5)) bitselector_2 (.in(B), .out(bitselector_2_out), .sel(3'b000));
  BitSelector #(.width(32), .group(5)) bitselector_3 (.in(B), .out(bitselector_3_out), .sel(3'b000));
  Negator #(.width(32)) negator_2 (.in(B), .out(negator_2_out));
  Adder #(.width(32)) adder_2 (.a(A), .b(B), .out(add));  // open: cin, cout
  assign and1 = A & B;  // AND_Gate and_1, 32 bits wide
  assign or1 = A | B;  // OR_Gate or_1, 32 bits wide
  assign xor1 = A ^ B;  // XOR_Gate xor_1, 32 bits wide
  Shifter #(.width(32), .shift("lr")) shifter_1 (.in(A), .\dist (bitselector_1_out), .out(srl1));
  Shifter #(.width(32), .shift("ar")) shifter_2 (.in(A), .\dist (bitselector_2_out), .out(sra1));
  Shifter #(.width(32)) shifter_3 (.in(A), .\dist (bitselector_3_out), .out(sll1));
  Subtractor #(.width(32)) subtractor_1 (.a(A), .b(B), .out({slt[0], sub}));  // open: bin, bout
  Divider #(.width(32)) divider_1 (.a(A), .b(B), .out(divu), .rem(remu));  // open: upper
  Multiplier #(.width(32)) multiplier_1 (.a(A), .b(B), .out(out_5), .cout(mulhu));  // open: cin
  Multiplexer #(.select(2), .width(32), .enable("false")) multiplexer_1 (
    .in0({32{1'b0}}), .in1(negator_2_out), .in2(negator_1_out), .in3(adder_1_out), .out(multiplexer_1_out),
    .sel({B[31], A[31]}));
  Adder #(.width(32)) adder_3 (.a(mulhu), .b(multiplexer_1_out), .out(out_7));  // open: cin, cout
  Multiplexer #(.select(4), .width(32), .enable("false")) multiplexer_2 (
    .in0(add), .in1(and1), .in2(or1), .in3(xor1), .in4(srl1), .in5(sra1), .in6(sll1),
    .in7({{31{1'b0}}, slt[0]}), .in8(divu), .in9(remu), .in10(out_5), .in11(mulhu), .in12({slt[0], sub}),
    .in13(B), .in14(out_7), .out(Result), .sel(ALUSel));  // open: in15
  Negator #(.width(32)) negator_3 (.in(out_7), .out(out_6));
  Negator #(.width(32)) negator_4 (.in(A), .out(negator_4_out));
  Adder #(.width(32)) adder_4 (.a(mulhu), .b(negator_4_out), .out(out_8));  // open: cin, cout

  // Other names for the same wires on the sheet: Asgn = A[31]; Bsgn = B[31]; mulh[31:0] = out_7; mult[31:0] = out_5;
  //   sub[31] = slt[0]

  // Notes on the sheet:
  //   INPUTS to your circuit
  //   DON'T CHANGE THE LOCATIONS OF THE INPUTS AND OUTPUTS!
  //   OUTPUT from your circuit
endmodule
