// Logisim project adder.circ as structural Verilog: 2 circuits, main circuit main
module main (
  input  in_1,
  output [7:0] out_2,
  output [7:0] out_3
);

  addmachine addmachine_1 (.in_1(in_1), .out_2(out_2), .out_3(out_3));
endmodule

module addmachine (
  input  in_1,
  output [7:0] out_2,
  output [7:0] out_3
);

  wire clock_1_out;

  Register register_1 (.D(out_3), .en(in_1), .clk(clock_1_out), .Q(out_2));  // open: clr
  Clock clock_1 (.out(clock_1_out));
  Adder adder_1 (.a(out_2), .b(8'h1), .out(out_3));  // open: cin, cout
endmodule
