// Logisim project part1.circ as structural Verilog: 6 circuits, main circuit main
module main (
  input  in_1,
  input  in_2,
  output out_3
);

  nand1 nand1_1 (.in_1(in_1), .in_2(in_2), .out_3(out_3));
endmodule

module nand1 (
  input  in_1,
  input  in_2,
  output out_3
);

  wire and_1_out;

  and and_1 (and_1_out, in_1, in_2);
  not not_1 (out_3, and_1_out);
endmodule

module NOR1 (
  input  in_1,
  input  in_2,
  output out_3
);

  wire or_1_out;

  or or_1 (or_1_out, in_1, in_2);
  not not_1 (out_3, or_1_out);
endmodule

module xor1 (
  input  in_1,
  input  in_2,
  output out_3
);

  wire and_1_out, and_2_out, not_1_out, not_2_out;

  not not_1 (not_1_out, in_1);
  not not_2 (not_2_out, in_2);
  and and_1 (and_1_out, in_1, not_2_out);
  and and_2 (and_2_out, not_1_out, in_2);
  or or_1 (out_3, and_1_out, and_2_out);
endmodule

module mux2to1 (
  input  Inp0,
  input  Inp1,
  input  Control,
  output out_4
);

  wire and_1_out, and_2_out, not_1_out;

  and and_1 (and_1_out, Inp0, not_1_out);
  and and_2 (and_2_out, Inp1, Control);
  not not_1 (not_1_out, Control);
  or or_1 (out_4, and_1_out, and_2_out);
endmodule

module mux4to1 (
  input  in_1,
  input  in_2,
  input  in_3,
  input  in_4,
  input  Control1,
  input  Control2,
  output out_7
);

  wire mux2to1_1_out_4, mux2to1_2_out_4;

  mux2to1 mux2to1_1 (.Inp0(in_1), .Inp1(in_2), .Control(Control1), .out_4(mux2to1_1_out_4));
  mux2to1 mux2to1_2 (.Inp0(in_3), .Inp1(in_4), .Control(Control1), .out_4(mux2to1_2_out_4));
  mux2to1 mux2to1_3 (.Inp0(mux2to1_1_out_4), .Inp1(mux2to1_2_out_4), .Control(Control2), .out_4(out_7));
endmodule
