// Logisim project part5_actual.circ as structural Verilog: 18 circuits, main circuit main
module main (
  input  [15:0] in_1,
  input  [3:0] in_2,
  output [15:0] out_3
);

  rotr rotr_1 (.InputA(in_1), .InputB(in_2), .out_3(out_3));
endmodule

module rotr (
  input  [15:0] InputA,
  input  [3:0] InputB,
  output [15:0] out_3
);

  wire [3:0] adder_1_out, not_1_out;
  wire [15:0] lshift1t_1_out_3, lshift2t_1_out_3, lshift4t_1_out_3, lshift8t_1_out_3, rshift1t_1_out_3,
       rshift2t_1_out_3, rshift4t_1_out_3, rshift8t_1_out_3;

  assign not_1_out = ~InputB;  // NOT_Gate not_1, 4 bits wide
  Adder #(.width(4)) adder_1 (.a(not_1_out), .b(4'b0001), .out(adder_1_out));  // open: cin, cout
  rshift1t rshift1t_1 (.in_1(InputB[0]), .in_2(InputA), .out_3(rshift1t_1_out_3));
  lshift1t lshift1t_1 (.in_1(adder_1_out[0]), .in_2(InputA), .out_3(lshift1t_1_out_3));
  rshift2t rshift2t_1 (.in_1(InputB[1]), .in_2(rshift1t_1_out_3), .out_3(rshift2t_1_out_3));
  lshift2t lshift2t_1 (.in_1(adder_1_out[1]), .in_2(lshift1t_1_out_3), .out_3(lshift2t_1_out_3));
  rshift4t rshift4t_1 (.in_1(InputB[2]), .in_2(rshift2t_1_out_3), .out_3(rshift4t_1_out_3));
  lshift4t lshift4t_1 (.in_1(adder_1_out[2]), .in_2(lshift2t_1_out_3), .out_3(lshift4t_1_out_3));
  rshift8t rshift8t_1 (.in_1(InputB[3]), .in_2(rshift4t_1_out_3), .out_3(rshift8t_1_out_3));
  lshift8t lshift8t_1 (.in_1(adder_1_out[3]), .in_2(lshift4t_1_out_3), .out_3(lshift8t_1_out_3));
  assign out_3 = rshift8t_1_out_3 | lshift8t_1_out_3;  // OR_Gate or_1, 16 bits wide
endmodule

module rshift1 (
  input  [15:0] in_1,
  output [15:0] out_2
);


  assign out_2 = {1'b0, in_1[15:1]};
endmodule

module rshift2 (
  input  [15:0] in_1,
  output [15:0] out_2
);

  wire [15:0] rshift1_1_out_2;

  rshift1 rshift1_1 (.in_1(in_1), .out_2(rshift1_1_out_2));
  rshift1 rshift1_2 (.in_1(rshift1_1_out_2), .out_2(out_2));
endmodule

module rshift4 (
  input  [15:0] in_1,
  output [15:0] out_2
);

  wire [15:0] rshift2_1_out_2;

  rshift2 rshift2_1 (.in_1(in_1), .out_2(rshift2_1_out_2));
  rshift2 rshift2_2 (.in_1(rshift2_1_out_2), .out_2(out_2));
endmodule

module rshift8 (
  input  [15:0] in_1,
  output [15:0] out_2
);

  wire [15:0] rshift4_1_out_2;

  rshift4 rshift4_1 (.in_1(in_1), .out_2(rshift4_1_out_2));
  rshift4 rshift4_2 (.in_1(rshift4_1_out_2), .out_2(out_2));
endmodule

module lshift1 (
  input  [15:0] in_1,
  output [15:0] out_2
);


  assign out_2 = {in_1[14:0], 1'b0};
endmodule

module lshift8 (
  input  [15:0] in_1,
  output [15:0] out_2
);

  wire [15:0] lshift4_1_out_2;

  lshift4 lshift4_1 (.in_1(in_1), .out_2(lshift4_1_out_2));
  lshift4 lshift4_2 (.in_1(lshift4_1_out_2), .out_2(out_2));
endmodule

module lshift4 (
  input  [15:0] in_1,
  output [15:0] out_2
);

  wire [15:0] lshift2_1_out_2;

  lshift2 lshift2_1 (.in_1(in_1), .out_2(lshift2_1_out_2));
  lshift2 lshift2_2 (.in_1(lshift2_1_out_2), .out_2(out_2));
endmodule

module lshift2 (
  input  [15:0] in_1,
  output [15:0] out_2
);

  wire [15:0] lshift1_1_out_2;

  lshift1 lshift1_1 (.in_1(in_1), .out_2(lshift1_1_out_2));
  lshift1 lshift1_2 (.in_1(lshift1_1_out_2), .out_2(out_2));
endmodule

module lshift2t (
  input  in_1,
  input  [15:0] in_2,
  output [15:0] out_3
);

  wire [15:0] and_1_out, and_2_out, bit_extender_1_out, lshift2_1_out_2, not_1_out;

  lshift2 lshift2_1 (.in_1(in_2), .out_2(lshift2_1_out_2));
  assign bit_extender_1_out = {{15{in_1}}, in_1};  // Bit_Extender bit_extender_1
  assign not_1_out = ~bit_extender_1_out;  // NOT_Gate not_1, 16 bits wide
  assign and_1_out = lshift2_1_out_2 & bit_extender_1_out;  // AND_Gate and_1, 16 bits wide
  assign and_2_out = not_1_out & in_2;  // AND_Gate and_2, 16 bits wide
  assign out_3 = and_2_out | and_1_out;  // OR_Gate or_1, 16 bits wide
endmodule

module lshift4t (
  input  in_1,
  input  [15:0] in_2,
  output [15:0] out_3
);

  wire [15:0] and_1_out, and_2_out, bit_extender_1_out, lshift4_1_out_2, not_1_out;

  lshift4 lshift4_1 (.in_1(in_2), .out_2(lshift4_1_out_2));
  assign bit_extender_1_out = {{15{in_1}}, in_1};  // Bit_Extender bit_extender_1
  assign not_1_out = ~bit_extender_1_out;  // NOT_Gate not_1, 16 bits wide
  assign and_1_out = lshift4_1_out_2 & bit_extender_1_out;  // AND_Gate and_1, 16 bits wide
  assign and_2_out = not_1_out & in_2;  // AND_Gate and_2, 16 bits wide
  assign out_3 = and_2_out | and_1_out;  // OR_Gate or_1, 16 bits wide
endmodule

module lshift8t (
  input  in_1,
  input  [15:0] in_2,
  output [15:0] out_3
);

  wire [15:0] and_1_out, and_2_out, bit_extender_1_out, lshift8_1_out_2, not_1_out;

  lshift8 lshift8_1 (.in_1(in_2), .out_2(lshift8_1_out_2));
  assign bit_extender_1_out = {{15{in_1}}, in_1};  // Bit_Extender bit_extender_1
  assign not_1_out = ~bit_extender_1_out;  // NOT_Gate not_1, 16 bits wide
  assign and_1_out = lshift8_1_out_2 & bit_extender_1_out;  // AND_Gate and_1, 16 bits wide
  assign and_2_out = not_1_out & in_2;  // AND_Gate and_2, 16 bits wide
  assign out_3 = and_2_out | and_1_out;  // OR_Gate or_1, 16 bits wide
endmodule

module lshift1t (
  input  in_1,
  input  [15:0] in_2,
  output [15:0] out_3
);

  wire [15:0] and_1_out, and_2_out, bit_extender_1_out, lshift1_1_out_2, not_1_out;

  lshift1 lshift1_1 (.in_1(in_2), .out_2(lshift1_1_out_2));
  assign bit_extender_1_out = {{15{in_1}}, in_1};  // Bit_Extender bit_extender_1
  assign not_1_out = ~bit_extender_1_out;  // NOT_Gate not_1, 16 bits wide
  assign and_1_out = lshift1_1_out_2 & bit_extender_1_out;  // AND_Gate and_1, 16 bits wide
  assign and_2_out = not_1_out & in_2;  // AND_Gate and_2, 16 bits wide
  assign out_3 = and_2_out | and_1_out;  // OR_Gate or_1, 16 bits wide
endmodule

module rshift1t (
  input  in_1,
  input  [15:0] in_2,
  output [15:0] out_3
);

  wire [15:0] and_1_out, and_2_out, bit_extender_1_out, not_1_out, rshift1_1_out_2;

  rshift1 rshift1_1 (.in_1(in_2), .out_2(rshift1_1_out_2));
  assign bit_extender_1_out = {{15{in_1}}, in_1};  // Bit_Extender bit_extender_1
  assign not_1_out = ~bit_extender_1_out;  // NOT_Gate not_1, 16 bits wide
  assign and_1_out = rshift1_1_out_2 & bit_extender_1_out;  // AND_Gate and_1, 16 bits wide
  assign and_2_out = not_1_out & in_2;  // AND_Gate and_2, 16 bits wide
  assign out_3 = and_2_out | and_1_out;  // OR_Gate or_1, 16 bits wide
endmodule

module rshift2t (
  input  in_1,
  input  [15:0] in_2,
  output [15:0] out_3
);

  wire [15:0] and_1_out, and_2_out, bit_extender_1_out, not_1_out, rshift2_1_out_2;

  rshift2 rshift2_1 (.in_1(in_2), .out_2(rshift2_1_out_2));
  assign bit_extender_1_out = {{15{in_1}}, in_1};  // Bit_Extender bit_extender_1
  assign not_1_out = ~bit_extender_1_out;  // NOT_Gate not_1, 16 bits wide
  assign and_1_out = rshift2_1_out_2 & bit_extender_1_out;  // AND_Gate and_1, 16 bits wide
  assign and_2_out = not_1_out & in_2;  // AND_Gate and_2, 16 bits wide
  assign out_3 = and_2_out | and_1_out;  // OR_Gate or_1, 16 bits wide
endmodule

module rshift4t (
  input  in_1,
  input  [15:0] in_2,
  output [15:0] out_3
);

  wire [15:0] and_1_out, and_2_out, bit_extender_1_out, not_1_out, rshift4_1_out_2;

  rshift4 rshift4_1 (.in_1(in_2), .out_2(rshift4_1_out_2));
  assign bit_extender_1_out = {{15{in_1}}, in_1};  // Bit_Extender bit_extender_1
  assign not_1_out = ~bit_extender_1_out;  // NOT_Gate not_1, 16 bits wide
  assign and_1_out = rshift4_1_out_2 & bit_extender_1_out;  // AND_Gate and_1, 16 bits wide
  assign and_2_out = not_1_out & in_2;  // AND_Gate and_2, 16 bits wide
  assign out_3 = and_2_out | and_1_out;  // OR_Gate or_1, 16 bits wide
endmodule

module rshift8t (
  input  in_1,
  input  [15:0] in_2,
  output [15:0] out_3
);

  wire [15:0] and_1_out, and_2_out, bit_extender_1_out, not_1_out, rshift8_1_out_2;

  rshift8 rshift8_1 (.in_1(in_2), .out_2(rshift8_1_out_2));
  assign bit_extender_1_out = {{15{in_1}}, in_1};  // Bit_Extender bit_extender_1
  assign not_1_out = ~bit_extender_1_out;  // NOT_Gate not_1, 16 bits wide
  assign and_1_out = rshift8_1_out_2 & bit_extender_1_out;  // AND_Gate and_1, 16 bits wide
  assign and_2_out = not_1_out & in_2;  // AND_Gate and_2, 16 bits wide
  assign out_3 = and_2_out | and_1_out;  // OR_Gate or_1, 16 bits wide
endmodule
