// Logisim project part5p1.circ as structural Verilog: 11 circuits, main circuit main
module main (
  input  [3:0] in_1,
  output [15:0] out_2
);

  rotr rotr_1 (.InputB(in_1), .out_3(out_2));  // open: InputA, out_4, out_5, out_6, out_7, out_8, out_9
endmodule

module rotr (
  input  [15:0] InputA,
  input  [3:0] InputB,
  output [15:0] out_3,
  output [15:0] out_4,
  output [15:0] out_5,
  output [15:0] out_6,
  output [15:0] out_7,
  output [15:0] out_8,
  output [15:0] out_9
);

  wire [3:0] subtractor_1_out, subtractor_2_out;
  wire [15:0] adder_1_out, adder_2_out, not_1_out;

  Subtractor #(.width(4)) subtractor_1 (.a(InputB), .b(4'b0001), .out(subtractor_1_out));  // open: bin, bout
  power2 power2_1 (.in_1(subtractor_1_out), .out_2(out_5));
  Subtractor #(.width(4)) subtractor_2 (.a(4'b1111), .b(InputB), .out(subtractor_2_out));  // open: bin, bout
  power2 power2_2 (.in_1(subtractor_2_out), .out_2(out_9));
  assign not_1_out = ~out_5;  // NOT_Gate not_1, 16 bits wide
  assign out_6 = InputA & out_5;  // AND_Gate and_1, 16 bits wide
  Adder #(.width(16)) adder_1 (.a(out_9), .b(16'h1), .out(adder_1_out));  // open: cin, cout
  assign out_3 = InputA & not_1_out;  // AND_Gate and_2, 16 bits wide
  Adder #(.width(16)) adder_2 (.a(out_5), .b(16'h1), .out(adder_2_out));  // open: cin, cout
  Multiplier #(.width(16)) multiplier_1 (.a(out_6), .b(adder_1_out), .out(out_8));  // open: cin, cout
  Divider #(.width(16)) divider_1 (.a(out_3), .b(adder_2_out), .out(out_4));  // open: upper, rem
  assign out_7 = out_4 | out_8;  // OR_Gate or_1, 16 bits wide
endmodule

module power2 (
  input  [3:0] in_1,
  output [15:0] out_2
);

  wire [15:0] undriven;

  Multiplexer #(.select(4), .width(16), .enable("false")) multiplexer_1 (
    .in0(16'h1), .in1(16'h3), .in2(16'h7), .in3(16'hf), .in4(undriven), .in5(16'h3f), .in6(16'h7f),
    .in7(16'hff), .in8(16'h1ff), .in9(16'h3ff), .in10(16'h7ff), .in11(16'hfff), .in12(16'h1fff),
    .in13(16'h3fff), .in14(16'h7fff), .in15({16{1'b0}}), .out(out_2), .sel(in_1));
endmodule

module rshift1 (
  input  [15:0] in_1,
  output [15:0] out_2
);


  assign out_2 = {1'b0, in_1[15:1]};
endmodule

module rshift2 (
  input  [15:0] in_1,
  output [15:0] out_2
);

  wire [15:0] rshift1_1_out_2;

  rshift1 rshift1_1 (.in_1(in_1), .out_2(rshift1_1_out_2));
  rshift1 rshift1_2 (.in_1(rshift1_1_out_2), .out_2(out_2));
endmodule

module rshift4 (
  input  [15:0] in_1,
  output [15:0] out_2
);

  wire [15:0] rshift2_1_out_2;

  rshift2 rshift2_1 (.in_1(in_1), .out_2(rshift2_1_out_2));
  rshift2 rshift2_2 (.in_1(rshift2_1_out_2), .out_2(out_2));
endmodule

module rshift8 (
  input  [15:0] in_1,
  output [15:0] out_2
);

  wire [15:0] rshift4_1_out_2;

  rshift4 rshift4_1 (.in_1(in_1), .out_2(rshift4_1_out_2));
  rshift4 rshift4_2 (.in_1(rshift4_1_out_2), .out_2(out_2));
endmodule

module lshift1 (
  input  [15:0] in_1,
  output [15:0] out_2
);


  assign out_2 = {in_1[14:0], 1'b0};
endmodule

module lshift8 (
  input  [15:0] in_1,
  output [15:0] out_2
);

  wire [15:0] lshift4_1_out_2;

  lshift4 lshift4_1 (.in_1(in_1), .out_2(lshift4_1_out_2));
  lshift4 lshift4_2 (.in_1(lshift4_1_out_2), .out_2(out_2));
endmodule

module lshift4 (
  input  [15:0] in_1,
  output [15:0] out_2
);

  wire [15:0] lshift2_1_out_2;

  lshift2 lshift2_1 (.in_1(in_1), .out_2(lshift2_1_out_2));
  lshift2 lshift2_2 (.in_1(lshift2_1_out_2), .out_2(out_2));
endmodule

module lshift2 (
  input  [15:0] in_1,
  output [15:0] out_2
);

  wire [15:0] lshift1_1_out_2;

  lshift1 lshift1_1 (.in_1(in_1), .out_2(lshift1_1_out_2));
  lshift1 lshift1_2 (.in_1(lshift1_1_out_2), .out_2(out_2));
endmodule
